# Fritzing sketch schematic (saved by Fritzing 0.9.5d)
breadboards: 1

parts:
  Part1 = Arduino Uno (Rev3)
  R1 = Resistor [tolerance=±5% resistance=220 package="0603 [SMD]"]
  LED = LED - 5mm [color="Red (633nm)" package="5 mm [THT]"]
  V1 = DC Power [voltage=5]

nets:
  N1: Part1.GND, LED.cathode, V1.V-
  N2: R1.Pin_0, V1.V+
  N3: R1.Pin_1, LED.anode
